# Fritzing sketch sketch-baiov2 (saved by Fritzing 0.9.4)
breadboards: 1

parts:
  Core = NodeMCU V3.0
  J1 = Screw terminal - 2 pins [package=THT]
  Reg = Voltage Regulator - 5V [package="DPak [SMD]"]
  C1_-_0_22uF = Capacitor [package=cap-pth-small]
  C2_-_0_1uF = Capacitor [package=cap-pth-small]
  MuX16_1 = Analog Digital MUX Breakout
  CSM = DFRobot Capacitive Soil Moisture Sensor V1.0 [part_number=SEN0193]
  R1 = Photocell (LDR) [package=THT]
  R2 = Resistor [tolerance=±5% resistance=10k package=THT]
  Water_Level_Sensor1 = Water Level Sensor
  Part1 = KY-019 5V Relay Module [package="Breakout board"]
  U4 = TRANSISTOR_NPN_2 [package=to-92]
  U1 = TRANSISTOR_NPN_2 [package=to-92]
  U2 = TRANSISTOR_NPN_2 [package=to-92]
  U5 = TRANSISTOR_NPN_2 [package=to-92]

nets:
  N1: Core.D0, Core.RST
  N2: Core.D1, MuX16_1.S0
  N3: Core.D2, MuX16_1.S1
  N4: Core.D3, U1.B
  N5: Core.D4, U2.B
  N6: Core.D5, U5.B
  N7: Core.D6, Part1.S
  N8: Core.D7, U4.B
  VCC: Core.Vin, Reg.output_voltage, C2_-_0_1uF.1, CSM.VCC, R1.pin_0, Water_Level_Sensor1.VCC, U4.E
  GND: Core.GND, J1.pin1, Reg.GND, C1_-_0_22uF.2, C2_-_0_1uF.2, R2.Pin_1, U1.C, U2.C, U5.C
  N9: Core.A0, MuX16_1.SIG
  N10: J1.pin2, Reg.input_voltage, C1_-_0_22uF.1
  N11: MuX16_1.C0, CSM.A
  N12: MuX16_1.C1, R1.pin_1, R2.Pin_0
  N13: MuX16_1.C2, Water_Level_Sensor1.SIG
  N14: MuX16_1.GND, U1.E
  N15: CSM.GND, U2.E
  N16: Water_Level_Sensor1.GND, U5.E

custom parts:
  NodeMCU V3.0: NodeMcu V3 Lua WIFI Development Board
  DFRobot Capacitive Soil Moisture Sensor V1.0: DFRobot Capacitive Soil Moisture Sensor V1.0 This product measures soil moisture levels by capacitive sensing, rather than resistive sensing like other types of moisture sensor. It is made of a corrosion resistant material giving it a long service life. Insert it into soil and impress your friends with the real-time soil moisture data! The product includes an on-board voltage regulator which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
  Water Level Sensor: A water level sensor. This sensor operates at 3V to 5V. The Sig (signal) pin outputs an analogue signal that is in proportion to the amount of water in contact with the sensor.
  KY-019 5V Relay Module: KY-019 5V Relay module, used to control AC circuits.
